# Fritzing sketch count-down-clock (saved by Fritzing 0.9.2b)
breadboards: 1

parts:
  Q1 = PNP-Transistor [package="TO92 [THT]"]
  Q2 = PNP-Transistor [package="TO92 [THT]"]
  Q3 = PNP-Transistor [package="TO92 [THT]"]
  Q4 = PNP-Transistor [package="TO92 [THT]"]
  Q5 = PNP-Transistor [package="TO92 [THT]"]
  Q6 = PNP-Transistor [package="TO92 [THT]"]
  R1 = Resistor [tolerance=±5% resistance=1k package=THT]
  R2 = Resistor [tolerance=±5% resistance=1k package=THT]
  R3 = Resistor [tolerance=±5% resistance=1k package=THT]
  R4 = Resistor [tolerance=±5% resistance=1k package=THT]
  R5 = Resistor [tolerance=±5% resistance=10k package=THT]
  R6 = Resistor [tolerance=±5% resistance=10k package=THT]
  LA1 = 2-Digit 7-Segment LED Display [package=THT]
  LA2 = 2-Digit 7-Segment LED Display [package=THT]
  HDSP1 = 2-Digit 7-Segment LED Display [package=THT]
  Part1 = Arduino Pro Mini v13
  R7 = Resistor [tolerance=±5% resistance=10 package=THT]
  R8 = Resistor [tolerance=±5% resistance=10 package=THT]
  R10 = Resistor [tolerance=±5% resistance=10 package=THT]
  R11 = Resistor [tolerance=±5% resistance=10 package=THT]
  R14 = Resistor [tolerance=±5% resistance=10 package=THT]
  R16 = Trimmer Potentiometer [maximum_resistance=10kΩ package=THT]
  R17 = Photocell (LDR) [package=THT]
  R18 = Resistor [tolerance=±5% resistance=4.7k package=THT]
  R19 = Resistor [tolerance=±5% resistance=10 package=THT]
  R20 = Resistor [tolerance=±5% resistance=10 package=THT]
  R21 = Resistor [tolerance=±5% resistance=10 package=THT]

nets:
  3.3V: Q1.E, Q2.E, Q3.E, Q4.E, Q5.E, Q6.E, Part1.VCC, R16.leg2
  N1: Q1.B, R3.Pin_0
  N2: Q1.C, LA2.ANODE2
  N3: Q2.B, R5.Pin_0
  N4: Q2.C, HDSP1.ANODE1
  N5: Q3.B, R6.Pin_0
  N6: Q3.C, HDSP1.ANODE2
  N7: Q4.B, R4.Pin_0
  N8: Q4.C, LA2.ANODE1
  N9: Q5.B, R1.Pin_0
  N10: Q5.C, LA1.ANODE2
  N11: Q6.B, R2.Pin_0
  N12: Q6.C, LA1.ANODE1
  N13: R1.Pin_1, Part1.D3_PWM
  N14: R2.Pin_1, Part1.D2
  N15: R3.Pin_1, Part1.D5_PWM
  N16: R4.Pin_1, Part1.D4
  N17: R5.Pin_1, Part1.A4
  N18: R6.Pin_1, Part1.A5
  N19: LA1.E1, LA1.E2, LA2.E1, LA2.E2, HDSP1.E1, HDSP1.E2, R20.Pin_0
  N20: LA1.D1, LA1.D2, LA2.D1, LA2.D2, HDSP1.D1, HDSP1.D2, R10.Pin_0
  N21: LA1.C1, LA1.C2, LA2.C1, LA2.C2, HDSP1.C1, HDSP1.C2, R19.Pin_0
  N22: LA1.DP1, LA1.DP2, LA2.DP1, LA2.DP2, HDSP1.DP1, HDSP1.DP2, R21.Pin_0
  N23: LA1.G2, LA1.G1, LA2.G2, LA2.G1, HDSP1.G2, HDSP1.G1, R14.Pin_0
  N24: LA1.B2, LA1.B1, LA2.B2, LA2.B1, HDSP1.B2, HDSP1.B1, R8.Pin_0
  N25: LA1.A2, LA1.A1, LA2.A2, LA2.A1, HDSP1.A2, HDSP1.A1, R7.Pin_0
  N26: LA1.F2, LA1.F1, LA2.F2, LA2.F1, HDSP1.F2, HDSP1.F1, R11.Pin_0
  GND: Part1.GND, R16.leg1, R18.Pin_0
  N27: Part1.A1, R17.pin_1, R18.Pin_1
  N28: Part1.A0, R16.wiper, R17.pin_0
  N29: Part1.D13/SCK, R21.Pin_1
  N30: Part1.D12/MISO, R14.Pin_1
  N31: Part1.D11_PWM/MOSI, R11.Pin_1
  N32: Part1.D10_PWM/SS, R20.Pin_1
  N33: Part1.D9_PWM, R10.Pin_1
  N34: Part1.D8, R19.Pin_1
  N35: Part1.D7, R8.Pin_1
  N36: Part1.D6_PWM, R7.Pin_1

notes:
  A1
  A2
  Count Down Clock, (C) Copyright 2015,  Farzad Battiwalla, 1
